# Fritzing sketch WiringDiagram (saved by Fritzing 0.9.4)
breadboards: 1

parts:
  Part1 = Arduino Nano (Rev3.0)
  R1 = Resistor [tolerance=±5% resistance=220 package=THT]
  J3 = male pin header, 4 pins [form="♂ (male)"]
  U1 = TEMPERATURE-SENSOR [package=to-92]  # not connected
  J5 = screw terminal, 3 pins

nets:
  N1: Part1.GND, J3.pin1, J5.pin3
  N2: Part1.D2, R1.Pin_1, J5.pin2
  N3: Part1.D10, J3.pin4
  N4: Part1.VIN, J3.pin2
  N5: Part1.3V3, R1.Pin_0, J5.pin1

notes:
  +12V
  GND
  FAN_PWM
  Temp Sensor Data
  +3V3
  4k7
